# Fritzing sketch PulseLedAnalogIn (saved by Fritzing 0.9.3b)
breadboards: 1

parts:
  Part1 = Arduino Uno (Rev3)
  LED1 = LED - 5mm [color="Red (633nm)" package="5 mm [THT]"]
  R1 = Resistor [tolerance=±5% resistance=220 package=THT]
  R2 = Rotary Potentiometer (Small) [maximum_resistance=100kΩ package=THT]

nets:
  N1: Part1.A0, R2.wiper
  N2: Part1.D3_PWM, R1.Pin_1
  N3: Part1.5V, R2.leg1
  N4: Part1.GND, R2.leg2
  N5: LED1.anode, R1.Pin_0
